// Logisim project idk.circ as structural Verilog: 1 circuit, main circuit main
module main (
  input  in_1,
  input  in_2,
  input  in_3
);

  wire transistor_1_out, transistor_3_out, transistor_5_out;

  LED led_1 (.in(transistor_1_out));
  Transistor transistor_1 (.in(1'b1), .out(transistor_1_out), .gate(in_3));
  Transistor #(.\type ("n")) transistor_2 (.in(1'b0), .out(transistor_1_out), .gate(in_3));
  Transistor transistor_3 (.in(1'b1), .out(transistor_3_out), .gate(in_2));
  LED led_2 (.in(transistor_3_out));
  Transistor #(.\type ("n")) transistor_4 (.in(transistor_5_out), .out(transistor_3_out), .gate(in_2));
  Transistor #(.\type ("n")) transistor_5 (.in(1'b0), .out(transistor_5_out), .gate(in_1));
  Transistor transistor_6 (.in(1'b1), .out(transistor_3_out), .gate(in_1));
endmodule
