// Logisim project BF_computer.circ as structural Verilog: 3 circuits, main circuit main
module main (
  input  [7:0] in_1
);

  wire and_1_out, and_2_out, and_3_out, and_4_out, and_5_out, button_1_out, clock_1_out, comparator_1_eq,
       controlled_buffer_1_out, decoder_1_out0, decoder_1_out1, decoder_1_out2, decoder_1_out3,
       decoder_1_out4, decoder_1_out5, decoder_1_out6, decoder_1_out7, HLT, or_1_out, or_2_out, or_3_out,
       or_4_out, or_5_out, or_6_out, sr_latch_1_q, sr_latch_2_nq, sr_latch_2_q, sr_latch_3_nq, sr_latch_3_q;
  wire [2:0] rom_1_data;
  wire [3:0] display_1_out_2, display_1_out_3, display_1_out_4;
  wire [7:0] adder_1_out, controlled_buffer_2_out, counter_1_q, counter_2_q, ram_1_dout, register_1_q,
       subtractor_1_out;

  Clock clock_1 (.out(clock_1_out));
  SR_Latch sr_latch_1 (.S(button_1_out), .R(HLT), .Q(sr_latch_1_q));  // open: NQ
  Button button_1 (.out(button_1_out));
  assign controlled_buffer_1_out = sr_latch_1_q ? clock_1_out : 1'bz;  // Controlled_Buffer controlled_buffer_1
  ROM #(.dataWidth(4)) rom_1 (.addr(counter_1_q), .data({HLT, rom_1_data}));
  Counter counter_1 (
    .Q(counter_1_q), .up(sr_latch_2_nq), .clk(controlled_buffer_1_out), .clr(button_1_out));  // open: load, D, count, carry
  SR_Latch sr_latch_2 (.S(and_2_out), .R(or_1_out), .NQ(sr_latch_2_nq), .Q(sr_latch_2_q));
  or or_1 (or_1_out, button_1_out, or_2_out);
  and and_1 (and_1_out, sr_latch_2_nq, decoder_1_out7, sr_latch_3_q);
  or or_2 (or_2_out, and_1_out, and_3_out);
  Decoder #(.select(3)) decoder_1 (
    .out0(decoder_1_out0), .out1(decoder_1_out1), .out2(decoder_1_out2), .out3(decoder_1_out3),
    .out4(decoder_1_out4), .out5(decoder_1_out5), .out6(decoder_1_out6), .out7(decoder_1_out7),
    .sel(rom_1_data));  // open: en
  and and_2 (and_2_out, decoder_1_out7, ~comparator_1_eq);  // AND_Gate
  and and_3 (and_3_out, sr_latch_2_q, decoder_1_out6, sr_latch_3_q);
  and and_4 (and_4_out, decoder_1_out6, comparator_1_eq);
  or or_3 (or_3_out, and_2_out, and_4_out);
  SR_Latch sr_latch_3 (.S(or_3_out), .R(or_4_out), .NQ(sr_latch_3_nq), .Q(sr_latch_3_q));
  or or_4 (or_4_out, or_2_out, button_1_out);
  or or_5 (or_5_out, decoder_1_out3, decoder_1_out2);
  Counter counter_2 (
    .count(or_5_out), .Q(counter_2_q), .up(decoder_1_out2), .clk(and_5_out), .clr(button_1_out));  // open: load, D, carry
  and and_5 (and_5_out, sr_latch_3_nq, controlled_buffer_1_out);
  or or_6 (or_6_out, decoder_1_out1, decoder_1_out0);
  RAM #(.clearpin("true"), .enables("line")) ram_1 (
    .addr(counter_2_q), .we(or_6_out), .clk(and_5_out), .din(controlled_buffer_2_out), .dout(ram_1_dout),
    .clr(button_1_out));
  assign controlled_buffer_2_out = decoder_1_out5 ? in_1 : 8'bz;  // Controlled_Buffer controlled_buffer_2
  Adder adder_1 (.a(ram_1_dout), .b(8'h1), .out(adder_1_out));  // open: cin, cout
  assign controlled_buffer_2_out = decoder_1_out1 ? subtractor_1_out : 8'bz;  // Controlled_Buffer controlled_buffer_3
  Subtractor subtractor_1 (.a(ram_1_dout), .b(8'h1), .out(subtractor_1_out));  // open: bin, bout
  assign controlled_buffer_2_out = decoder_1_out0 ? adder_1_out : 8'bz;  // Controlled_Buffer controlled_buffer_4
  Comparator #(.mode("unsigned")) comparator_1 (.a({8{1'b0}}), .b(ram_1_dout), .eq(comparator_1_eq));  // open: gt, lt
  Register register_1 (.D(ram_1_dout), .en(decoder_1_out4), .Q(register_1_q), .clk(decoder_1_out4), .clr(button_1_out));
  Display display_1 (.in_1(register_1_q), .out_2(display_1_out_2), .out_3(display_1_out_3), .out_4(display_1_out_4));
  Hex_Digit_Display hex_digit_display_1 (.value(display_1_out_2));  // open: dp
  Hex_Digit_Display hex_digit_display_2 (.value(display_1_out_3));  // open: dp
  Hex_Digit_Display hex_digit_display_3 (.value(display_1_out_4));  // open: dp
  TTY tty_1 (.data(register_1_q[6:0]), .clk(decoder_1_out4), .we(decoder_1_out4), .clr(button_1_out));

  // Notes on the sheet:
  //   contents of rom_1 (hex, n*v repeats v):
  //   2 8*0 6 3 9*0 2 1 7 3 4 2 4*0 6 3 7*0 2 1 7 3 0 4 7*0 4 4 0 0 0 4 2 2 6*0 6 3 7*0 2 1 7 3 0 0 4 12*1
  //   4 2 6*0 6 3 9*0 2 1 7 3 0 4 3 4 0 0 0 4 6*1 4 8*1 4 2 2 2 4*0 6 3 8*0 2 1 7 3 0 4 8
  //   Forewards
  //   searching
endmodule

module Display (
  input  [7:0] in_1,
  output [3:0] out_2,
  output [3:0] out_3,
  output [3:0] out_4
);

  // Binary_to_BCD_converter #(.binvalue(8)) binary_to_bcd_converter_1: pin names not known; wires that end beside it: in_1, out_2, out_3, out_4
endmodule

module SR_Latch (
  input  S,
  input  R,
  output NQ,
  output Q
);

  nor nor_1 (NQ, Q, S);
  nor nor_2 (Q, R, NQ);
endmodule
