// Logisim project incrementer.circ as structural Verilog: 2 circuits, main circuit main
module main (
  input  reset,
  input  [3:0] data
);

  wire clock_1_out, full_adder_1_cout, full_adder_1_sum, full_adder_2_cout, full_adder_2_sum,
       full_adder_3_cout, full_adder_3_sum, full_adder_4_sum, multiplexer_1_out, multiplexer_2_out,
       multiplexer_3_out, multiplexer_4_out, not_1_out;
  wire [3:0] d_ff_1_q;

  Clock clock_1 (.out(clock_1_out));
  // Probe on d_ff_1_q
  not not_1 (not_1_out, reset);
  Multiplexer multiplexer_1 (.in0(data[0]), .in1(full_adder_1_sum), .out(multiplexer_1_out), .sel(not_1_out));
  full_adder full_adder_1 (.y(d_ff_1_q[0]), .cin(1'b0), .x(1'b1), .sum(full_adder_1_sum), .cout(full_adder_1_cout));
  D_Flip_Flop d_ff_1 (.clk(clock_1_out), .D(multiplexer_1_out), .Q(d_ff_1_q[0]));  // open: Qn, preset, reset
  Multiplexer multiplexer_2 (.in0(data[1]), .in1(full_adder_2_sum), .out(multiplexer_2_out), .sel(not_1_out));
  full_adder full_adder_2 (
    .y(d_ff_1_q[1]), .cin(full_adder_1_cout), .x(1'b0), .sum(full_adder_2_sum), .cout(full_adder_2_cout));
  D_Flip_Flop d_ff_2 (.clk(clock_1_out), .D(multiplexer_2_out), .Q(d_ff_1_q[1]));  // open: Qn, preset, reset
  full_adder full_adder_3 (
    .y(d_ff_1_q[2]), .cin(full_adder_2_cout), .x(1'b0), .sum(full_adder_3_sum), .cout(full_adder_3_cout));
  Multiplexer multiplexer_3 (.in0(data[2]), .in1(full_adder_3_sum), .out(multiplexer_3_out), .sel(not_1_out));
  full_adder full_adder_4 (.y(d_ff_1_q[3]), .cin(full_adder_3_cout), .x(1'b0), .sum(full_adder_4_sum));  // open: cout
  D_Flip_Flop d_ff_3 (.clk(clock_1_out), .D(multiplexer_3_out), .Q(d_ff_1_q[2]));  // open: Qn, preset, reset
  Multiplexer multiplexer_4 (.in0(data[3]), .in1(full_adder_4_sum), .out(multiplexer_4_out), .sel(not_1_out));
  D_Flip_Flop d_ff_4 (.clk(clock_1_out), .D(multiplexer_4_out), .Q(d_ff_1_q[3]));  // open: Qn, preset, reset
endmodule

module full_adder (
  input  cin,
  input  x,
  input  y,
  output cout,
  output sum
);

  Adder #(.width(1)) adder_1 (.a(x), .b(y), .out(sum), .cin(cin), .cout(cout));
endmodule
