// Logisim project latches_and_flip_flops.circ as structural Verilog: 3 circuits, main circuit main
module main (
  input  Data,
  input  in_2,
  input  in_3
);

  wire and_1_out, and_2_out, and_3_out, and_4_out, and_5_out, and_6_out, and_7_out, and_8_out, and_9_out,
       and_10_out, and_11_out, and_12_out, and_13_out, and_14_out, and_15_out, and_16_out, and_17_out,
       and_18_out, and_19_out, and_20_out, and_21_out, and_22_out, and_23_out, button_1_out, button_2_out,
       clock_1_out, clock_2_out, clock_3_out, clock_4_out, full_adder_1_cout, full_adder_1_sum,
       full_adder_2_cout, full_adder_2_sum, full_adder_3_cout, full_adder_3_sum, full_adder_4_cout,
       full_adder_4_sum, full_adder_5_cout, full_adder_5_sum, full_adder_6_cout, full_adder_6_sum,
       full_adder_7_cout, full_adder_7_sum, full_adder_8_cout, full_adder_8_sum, full_adder_9_cout,
       full_adder_9_sum, full_adder_10_cout, full_adder_10_sum, full_adder_11_sum, full_adder_12_sum,
       not_1_out, not_2_out, not_3_out, not_4_out, not_5_out, not_6_out, not_7_out, not_8_out, not_9_out,
       or_1_out, or_2_out, or_3_out, or_4_out, or_5_out, or_6_out, or_7_out, or_8_out, R_out, Reset_out,
       S_out, Save_out;
  wire [3:0] d_ff_1_q, d_ff_5_q, d_ff_6_q;

  Button Save (.out(Save_out));
  not not_1 (not_1_out, Data);
  Clock clock_1 (.out(clock_1_out));
  not not_2 (not_2_out, clock_1_out);
  Button Reset (.out(Reset_out));
  Clock clock_2 (.out(clock_2_out));
  // Probe on d_ff_1_q
  Button S (.out(S_out));
  Button R (.out(R_out));
  and and_1 (and_1_out, Save_out, Data);
  and and_2 (and_2_out, Save_out, not_1_out);
  and and_3 (and_3_out, not_2_out, in_3);
  or or_1 (or_1_out, and_3_out, and_7_out);
  and and_4 (and_4_out, not_2_out, ~in_3);  // AND_Gate
  not not_3 (not_3_out, Reset_out);
  or or_2 (or_2_out, S_out, and_5_out);
  and and_5 (and_5_out, or_2_out, not_4_out);
  not not_4 (not_4_out, R_out);
  or or_3 (or_3_out, and_1_out, and_6_out);
  and and_6 (and_6_out, or_3_out, not_5_out);
  not not_5 (not_5_out, and_2_out);
  and and_7 (and_7_out, or_1_out, ~and_4_out);  // AND_Gate
  not not_6 (not_6_out, not_2_out);
  and and_8 (and_8_out, not_3_out, or_4_out);
  or or_4 (or_4_out, and_15_out, full_adder_1_sum);
  full_adder full_adder_1 (.y(d_ff_1_q[0]), .Cin(1'b0), .x(1'b1), .Cout(full_adder_1_cout), .sum(full_adder_1_sum));
  D_Flip_Flop d_ff_1 (.clk(clock_2_out), .D(and_8_out), .Q(d_ff_1_q[0]));  // open: Qn, preset, reset
  LED led_1 (.in(and_5_out));
  LED led_2 (.in(and_6_out));
  and and_9 (and_9_out, not_6_out, and_7_out);
  and and_10 (and_10_out, not_6_out, ~and_7_out);  // AND_Gate
  and and_11 (and_11_out, not_3_out, or_5_out);
  or or_5 (or_5_out, and_15_out, full_adder_2_sum);
  full_adder full_adder_2 (
    .y(d_ff_1_q[1]), .Cin(full_adder_1_cout), .x(1'b0), .Cout(full_adder_2_cout), .sum(full_adder_2_sum));
  D_Flip_Flop d_ff_2 (.clk(clock_2_out), .D(and_11_out), .Q(d_ff_1_q[1]));  // open: Qn, preset, reset
  or or_6 (or_6_out, and_9_out, and_12_out);
  and and_12 (and_12_out, or_6_out, ~and_10_out);  // AND_Gate
  and and_13 (and_13_out, not_3_out, or_7_out);
  or or_7 (or_7_out, and_15_out, full_adder_3_sum);
  full_adder full_adder_3 (
    .y(d_ff_1_q[2]), .Cin(full_adder_2_cout), .x(1'b0), .Cout(full_adder_3_cout), .sum(full_adder_3_sum));
  D_Flip_Flop d_ff_3 (.clk(clock_2_out), .D(and_13_out), .Q(d_ff_1_q[2]));  // open: Qn, preset, reset
  LED led_3 (.in(and_12_out));
  and and_14 (and_14_out, not_3_out, or_8_out);
  or or_8 (or_8_out, and_15_out, full_adder_4_sum);
  full_adder full_adder_4 (
    .y(d_ff_1_q[3]), .Cin(full_adder_3_cout), .x(1'b0), .Cout(full_adder_4_cout), .sum(full_adder_4_sum));
  D_Flip_Flop d_ff_4 (.clk(clock_2_out), .D(and_14_out), .Q(d_ff_1_q[3]));  // open: Qn, preset, reset
  and and_15 (and_15_out, not_3_out, full_adder_4_cout);
  Button button_1 (.out(button_1_out));
  Clock clock_3 (.out(clock_3_out));
  // Probe on d_ff_5_q
  Button button_2 (.out(button_2_out));
  Clock clock_4 (.out(clock_4_out));
  // Probe on d_ff_6_q
  not not_7 (not_7_out, button_1_out);
  not not_8 (not_8_out, in_2);
  full_adder full_adder_5 (
    .y(d_ff_5_q[0]), .Cin(in_2), .x(not_8_out), .Cout(full_adder_5_cout), .sum(full_adder_5_sum));
  not not_9 (not_9_out, button_2_out);
  full_adder full_adder_6 (.y(d_ff_6_q[0]), .Cin(1'b0), .x(1'b1), .Cout(full_adder_6_cout), .sum(full_adder_6_sum));
  and and_16 (and_16_out, not_7_out, full_adder_5_sum);
  full_adder full_adder_7 (
    .y(d_ff_5_q[1]), .Cin(full_adder_5_cout), .x(in_2), .Cout(full_adder_7_cout), .sum(full_adder_7_sum));
  D_Flip_Flop d_ff_5 (.clk(clock_3_out), .D(and_16_out), .Q(d_ff_5_q[0]));  // open: Qn, preset, reset
  and and_17 (and_17_out, not_9_out, full_adder_6_sum);
  full_adder full_adder_8 (
    .y(d_ff_6_q[1]), .Cin(full_adder_6_cout), .x(1'b0), .Cout(full_adder_8_cout), .sum(full_adder_8_sum));
  D_Flip_Flop d_ff_6 (.clk(clock_4_out), .D(and_17_out), .Q(d_ff_6_q[0]));  // open: Qn, preset, reset
  and and_18 (and_18_out, not_7_out, full_adder_7_sum);
  full_adder full_adder_9 (
    .y(d_ff_5_q[2]), .Cin(full_adder_7_cout), .x(in_2), .Cout(full_adder_9_cout), .sum(full_adder_9_sum));
  D_Flip_Flop d_ff_7 (.clk(clock_3_out), .D(and_18_out), .Q(d_ff_5_q[1]));  // open: Qn, preset, reset
  and and_19 (and_19_out, not_9_out, full_adder_8_sum);
  D_Flip_Flop d_ff_8 (.clk(clock_4_out), .D(and_19_out), .Q(d_ff_6_q[1]));  // open: Qn, preset, reset
  and and_20 (and_20_out, not_7_out, full_adder_9_sum);
  D_Flip_Flop d_ff_9 (.clk(clock_3_out), .D(and_20_out), .Q(d_ff_5_q[2]));  // open: Qn, preset, reset
  and and_21 (and_21_out, not_9_out, full_adder_10_sum);
  full_adder full_adder_10 (
    .y(d_ff_6_q[2]), .Cin(full_adder_8_cout), .x(1'b0), .Cout(full_adder_10_cout), .sum(full_adder_10_sum));
  D_Flip_Flop d_ff_10 (.clk(clock_4_out), .D(and_21_out), .Q(d_ff_6_q[2]));  // open: Qn, preset, reset
  and and_22 (and_22_out, not_7_out, full_adder_11_sum);
  full_adder full_adder_11 (.y(d_ff_5_q[3]), .Cin(full_adder_9_cout), .x(in_2), .sum(full_adder_11_sum));  // open: Cout
  D_Flip_Flop d_ff_11 (.clk(clock_3_out), .D(and_22_out), .Q(d_ff_5_q[3]));  // open: Qn, preset, reset
  and and_23 (and_23_out, not_9_out, full_adder_12_sum);
  full_adder full_adder_12 (
    .y(d_ff_6_q[3]), .Cin(full_adder_10_cout), .x(1'b0), .sum(full_adder_12_sum));  // open: Cout
  D_Flip_Flop d_ff_12 (.clk(clock_4_out), .D(and_23_out), .Q(d_ff_6_q[3]));  // open: Qn, preset, reset

  // Notes on the sheet:
  //   saturating counter
  //   subtracting counter
  //   normal counter
endmodule

module full_adder (
  input  Cin,
  input  x,
  input  y,
  output Cout,
  output sum
);

  Adder #(.width(1)) adder_1 (.a(x), .b(y), .out(sum), .cin(Cin), .cout(Cout));
endmodule

module D_latch (
  input  in_1
);

  wire button_1_out, nor_1_out, nor_2_out, nor_3_out, nor_4_out;

  Button button_1 (.out(button_1_out));
  nor nor_1 (nor_1_out, ~button_1_out, ~in_1);  // NOR_Gate
  nor nor_2 (nor_2_out, nor_1_out, nor_3_out);
  nor nor_3 (nor_3_out, nor_2_out, nor_4_out);
  nor nor_4 (nor_4_out, button_1_out, ~in_1);  // NOR_Gate
  LED led_1 (.in(nor_3_out));
endmodule
